// Logisim project 1222440_1220619_1220039 (1) (1).circ as structural Verilog: 4 circuits, main circuit Alu
module main (
  input  [1:0] in_1
);

  wire _0, _1, _2, _3, _4, and_1_out, and_2_out, and_3_out, and_4_out, and_5_out, and_6_out, and_7_out,
       and_8_out, and_9_out, and_10_out, branchSe, clk, \dist , equal, ext, greater_than,
       greater_thanOrEqual, jumpSe, less_than, memRead, memWrite, not_1_out, not_2_out, not_3_out, not_4_out,
       not_5_out, not_6_out, not_9_out, not_10_out, not_11_out, not_12_out, not_13_out, notEqual, RW;
  wire [1:0] Bsel, f, pcCalc, wbData;
  wire [2:0] Imm3, multiplexer_4_out;
  wire [3:0] ALUOP;
  wire [4:0] shifter_2_out;
  wire [4:2] Imm5;
  wire [7:5] Imm11;
  wire [10:0] shifter_1_out, shifter_3_out;
  wire [19:0] bit_extender_1_out, bit_extender_2_out, branch, jump, multiplexer_1_out, multiplexer_2_out,
       multiplexer_3_out, pc, PC_2;
  wire [31:0] alu_1_result, bit_extender_5_out, bit_extender_7_out, multiplexer_5_out, multiplexer_6_out,
       ram_1_data, reg_file_1_busy, reg_file_1_busz, result, sign, sign_extend__Imm3_Imm2, zero;

  and and_1 (and_1_out, _4, _3, not_1_out, _1, not_2_out);
  not not_1 (not_1_out, _2);
  and and_2 (and_2_out, and_1_out, greater_thanOrEqual);
  not not_2 (not_2_out, _0);
  and and_3 (and_3_out, _4, _3, not_3_out, _1, not_4_out);
  not not_3 (not_3_out, _2);
  or or_1 (branchSe, and_2_out, and_4_out, and_6_out, and_7_out);
  and and_4 (and_4_out, and_3_out, less_than);
  not not_4 (not_4_out, _0);
  Clock clock_1 (.out(clk));
  not not_5 (not_5_out, _4);
  Multiplexer #(.width(20), .enable("false")) multiplexer_1 (
    .in0(PC_2), .in1(branch), .out(multiplexer_1_out), .sel(branchSe));
  Shifter #(.width(11)) shifter_1 (.in({Imm3, Imm11, Imm5, f}), .\dist (4'b0001), .out(shifter_1_out));
  Shifter #(.width(5)) shifter_2 (.in({Imm5, f}), .\dist (3'b001), .out(shifter_2_out));
  and and_5 (and_5_out, not_5_out, _3, _2, _1, _0);
  Multiplexer #(.width(20), .enable("false")) multiplexer_2 (
    .in0(jump), .in1(PC_2), .out(multiplexer_2_out), .sel(jumpSe));
  assign bit_extender_1_out = {{9{1'b0}}, shifter_1_out};  // Bit_Extender bit_extender_1
  assign bit_extender_2_out = {{15{1'b0}}, shifter_2_out};  // Bit_Extender bit_extender_2
  assign zero = {{27{1'b0}}, {Imm5, f}};  // Bit_Extender bit_extender_3
  assign sign = {{27{Imm5[4]}}, {Imm5, f}};  // Bit_Extender bit_extender_4
  and and_6 (and_6_out, and_5_out, notEqual);
  not not_6 (not_6_out, _4);
  Adder #(.width(20)) adder_1 (.a(pc), .b(bit_extender_1_out), .out(jump));  // open: cin, cout
  Adder #(.width(20)) adder_2 (.a(pc), .b(bit_extender_2_out), .out(branch));  // open: cin, cout
  and and_7 (and_7_out, and_8_out, equal);
  and and_8 (and_8_out, not_6_out, _3, _2, _1, _0);
  Multiplexer #(.select(2), .width(20), .enable("false")) multiplexer_3 (
    .in0(multiplexer_1_out), .in1(PC_2), .in2(multiplexer_2_out), .out(multiplexer_3_out), .sel(pcCalc));  // open: in3
  Register #(.width(20)) u_PC (.D(multiplexer_3_out), .en(1'b1), .Q(pc), .clk(clk));  // open: clr
  Comparator #(.width(3)) comparator_1 (.a(Imm3), .b(Imm11), .gt(greater_than), .eq(equal), .lt(less_than));
  not not_7 (greater_thanOrEqual, less_than);
  controlUnit controlunit_1 (
    .opCode({_4, _3, _2, _1, _0}), .pcCalc(pcCalc), .\dist (\dist ), .RW(RW), .ext(ext), .Bsel(Bsel),
    .memoryWrite(memWrite), .memoryRead(memRead), .WBdata(wbData), .ALUop(ALUOP), .f(in_1));
  Adder #(.width(20)) adder_3 (.a(pc), .b(20'h2), .out(PC_2));  // open: cin, cout
  not not_8 (notEqual, equal);
  ROM #(.addrWidth(20), .dataWidth(16)) rom_1 (
    .addr(pc), .data({_4, _3, _2, _1, _0, Imm3, Imm11, Imm5, f}));  // open: sel
  Multiplexer #(.width(3), .enable("false")) multiplexer_4 (
    .in0(Imm3), .in1(3'b111), .out(multiplexer_4_out), .sel(\dist ));
  reg_File reg_file_1 (
    .busX(result), .Ry(Imm11), .RZ(Imm5), .RX(multiplexer_4_out), .regWrite(RW), .BusY(reg_file_1_busy),
    .clk(clk), .BusZ(reg_file_1_busz));
  Multiplexer #(.width(32), .enable("false")) multiplexer_5 (
    .in0(zero), .in1(sign), .out(multiplexer_5_out), .sel(ext));
  assign bit_extender_5_out = {{21{1'b0}}, shifter_3_out};  // Bit_Extender bit_extender_5
  Shifter #(.width(11)) shifter_3 (.in({Imm3, Imm11, Imm5, f}), .\dist (4'b0001), .out(shifter_3_out));
  and and_9 (and_9_out, _4, not_10_out, _2, not_9_out, _0);
  not not_9 (not_9_out, _1);
  not not_10 (not_10_out, _3);
  Multiplexer #(.select(2), .width(32), .enable("false")) multiplexer_6 (
    .in0(reg_file_1_busz), .in1(sign_extend__Imm3_Imm2), .in2(multiplexer_5_out), .in3(bit_extender_5_out),
    .out(multiplexer_6_out), .sel(Bsel));
  or or_2 (jumpSe, and_9_out, and_10_out);
  Alu alu_1 (.A(reg_file_1_busy), .B(multiplexer_6_out), .Result(alu_1_result));  // open: ALU_OPCODE
  and and_10 (and_10_out, _4, not_12_out, _2, not_11_out, not_13_out);
  not not_11 (not_11_out, _1);
  not not_12 (not_12_out, _3);
  assign sign_extend__Imm3_Imm2 = {{27{Imm3[2]}}, {Imm3, f}};  // Bit_Extender bit_extender_6
  not not_13 (not_13_out, _0);
  RAM #(.addrWidth(20), .dataWidth(32), .bus("separate")) ram_1 (
    .addr(alu_1_result[19:0]), .din(reg_file_1_busz), .data(ram_1_data), .str(memWrite), .clk(clk),
    .ld(memRead));  // open: sel, clr
  assign bit_extender_7_out = {{12{1'b0}}, PC_2};  // Bit_Extender bit_extender_7
  Multiplexer #(.select(2), .width(32), .enable("false")) multiplexer_7 (
    .in0(alu_1_result), .in1(ram_1_data), .in2(bit_extender_7_out), .out(result), .sel(wbData));  // open: in3

  // Other names for the same wires on the sheet: Imm11 (some bits) = {Imm3, Imm5, f}; z[2:0] = Imm5; y[2:0] = Imm11;
  //   op[4:0] = {_4, _3, _2, _1, _0}; Imm2[1:0] = f; Imm5[1:0] = f; x[2:0] = Imm3

  // Notes on the sheet:
  //   contents of rom_1 (hex, n*v repeats v):
  //   468 565 32a 744 b44 e65 d6a 973 1445 1dc5 2465 2de5 3325 3ca5 2a88 4b25 5325 5aa5 65c5 6945 7685
  //   7a65 85c5 8945 9645 9b6e a352 ab36
endmodule

// ALU
module Alu (
  input  [31:0] A,
  input  [31:0] B,
  input  [3:0] ALU_OPCODE,
  output [31:0] Result
);

  wire comparator_1_eq, comparator_2_lt;
  wire [31:0] adder_1_out, adder_2_out, AND_Gate_out, bit_extender_1_out, bit_extender_2_out, CAND_out,
       not_1_out, OR_Gate_out, shifter_1_out, shifter_2_out, shifter_3_out, shifter_4_out, XOR_Gate_out;

  assign not_1_out = ~A;  // NOT_Gate not_1, 32 bits wide
  assign AND_Gate_out = A & B;  // AND_Gate AND_Gate, 32 bits wide
  assign OR_Gate_out = A | B;  // OR_Gate OR_Gate, 32 bits wide
  assign CAND_out = not_1_out & B;  // AND_Gate CAND, 32 bits wide
  Adder #(.width(32)) adder_1 (.a(A), .b(B), .out(adder_1_out));  // open: cin, cout
  Adder #(.width(32)) adder_2 (.a(not_1_out), .b(B), .out(adder_2_out));  // open: cin, cout
  Comparator #(.width(32), .mode("unsigned")) comparator_1 (.a(A), .b(B), .eq(comparator_1_eq));  // open: gt, lt
  Comparator #(.width(32), .mode("unsigned")) comparator_2 (.a(A), .b(B), .lt(comparator_2_lt));  // open: gt, eq
  Shifter #(.width(32), .shift("ar")) shifter_1 (.in(A), .\dist (B[4:0]), .out(shifter_1_out));
  Shifter #(.width(32), .shift("rr")) shifter_2 (.in(A), .\dist (B[4:0]), .out(shifter_2_out));
  Shifter #(.width(32), .shift("lr")) shifter_3 (.in(A), .\dist (B[4:0]), .out(shifter_3_out));
  Shifter #(.width(32)) shifter_4 (.in(A), .\dist (B[4:0]), .out(shifter_4_out));
  assign XOR_Gate_out = A ^ B;  // XOR_Gate XOR_Gate, 32 bits wide
  assign bit_extender_1_out = {{31{1'b0}}, comparator_1_eq};  // Bit_Extender bit_extender_1
  assign bit_extender_2_out = {{31{1'b0}}, comparator_2_lt};  // Bit_Extender bit_extender_2
  Multiplexer #(.select(4), .width(32), .enable("false")) multiplexer_1 (
    .in0(XOR_Gate_out), .in1(AND_Gate_out), .in2(OR_Gate_out), .in3(CAND_out), .in4(adder_1_out),
    .in5(adder_2_out), .in6(bit_extender_1_out), .in7(bit_extender_2_out), .in8(shifter_1_out),
    .in9(shifter_2_out), .in10(shifter_3_out), .in11(shifter_4_out), .out(Result), .sel(ALU_OPCODE));  // open: in12, in13, in14, in15
endmodule

module reg_File (
  input  [31:0] busX,
  input  [2:0] Ry,
  input  [2:0] RZ,
  input  [2:0] RX,
  input  regWrite,
  input  clk,
  output [31:0] BusY,
  output [31:0] BusZ
);

  wire and_1_out, and_2_out, and_3_out, and_4_out, and_5_out, and_6_out, and_7_out, decoder_1_out0,
       decoder_2_out0, decoder_2_out1, decoder_2_out2, decoder_2_out3, decoder_2_out4, decoder_2_out5,
       decoder_2_out6, decoder_2_out7, decoder_3_out0, decoder_3_out1, decoder_3_out2, decoder_3_out3,
       decoder_3_out4, decoder_3_out5, decoder_3_out6, decoder_3_out7, R1, R2, R3, R4, R5, R6, R7;
  wire [31:0] R1_q, R2_q, R3_q, R4_q, R5_q, R6_q, R7_q;

  Decoder #(.select(3), .enable("false")) decoder_1 (
    .out0(decoder_1_out0), .out1(R1), .out2(R2), .out3(R3), .out4(R4), .out5(R5), .out6(R6), .out7(R7),
    .sel(RX));
  and and_1 (and_1_out, R1, regWrite);
  and and_2 (and_2_out, R2, regWrite);
  and and_3 (and_3_out, R3, regWrite);
  and and_4 (and_4_out, R4, regWrite);
  and and_5 (and_5_out, R5, regWrite);
  and and_6 (and_6_out, R6, regWrite);
  and and_7 (and_7_out, R7, regWrite);
  Register #(.width(32)) u_R1 (.D(busX), .en(and_1_out), .Q(R1_q), .clk(clk));  // open: clr
  assign BusY = decoder_2_out0 ? {32{1'b0}} : 32'bz;  // Controlled_Buffer controlled_buffer_1
  Register #(.width(32)) u_R2 (.D(busX), .en(and_2_out), .Q(R2_q), .clk(clk));  // open: clr
  assign BusY = decoder_2_out2 ? R2_q : 32'bz;  // Controlled_Buffer controlled_buffer_2
  Register #(.width(32)) u_R3 (.D(busX), .en(and_3_out), .Q(R3_q), .clk(clk));  // open: clr
  Register #(.width(32)) u_R4 (.D(busX), .en(and_4_out), .Q(R4_q), .clk(clk));  // open: clr
  assign BusY = decoder_2_out4 ? R4_q : 32'bz;  // Controlled_Buffer controlled_buffer_3
  assign BusY = decoder_2_out5 ? R5_q : 32'bz;  // Controlled_Buffer controlled_buffer_4
  Register #(.width(32)) u_R5 (.D(busX), .en(and_5_out), .Q(R5_q), .clk(clk));  // open: clr
  Register #(.width(32)) u_R6 (.D(busX), .en(and_6_out), .Q(R6_q), .clk(clk));  // open: clr
  Register #(.width(32)) u_R7 (.D(busX), .en(and_7_out), .Q(R7_q), .clk(clk));  // open: clr
  assign BusY = decoder_2_out1 ? R1_q : 32'bz;  // Controlled_Buffer controlled_buffer_5
  assign BusY = decoder_2_out3 ? R3_q : 32'bz;  // Controlled_Buffer controlled_buffer_6
  assign BusY = decoder_2_out6 ? R6_q : 32'bz;  // Controlled_Buffer controlled_buffer_7
  assign BusY = decoder_2_out7 ? R7_q : 32'bz;  // Controlled_Buffer controlled_buffer_8
  Decoder #(.select(3), .enable("false")) decoder_2 (
    .out0(decoder_2_out0), .out1(decoder_2_out1), .out2(decoder_2_out2), .out3(decoder_2_out3),
    .out4(decoder_2_out4), .out5(decoder_2_out5), .out6(decoder_2_out6), .out7(decoder_2_out7), .sel(Ry));
  assign BusZ = decoder_3_out0 ? {32{1'b0}} : 32'bz;  // Controlled_Buffer controlled_buffer_9
  assign BusZ = decoder_3_out1 ? R1_q : 32'bz;  // Controlled_Buffer controlled_buffer_10
  assign BusZ = decoder_3_out7 ? R7_q : 32'bz;  // Controlled_Buffer controlled_buffer_11
  Decoder #(.select(3), .enable("false")) decoder_3 (
    .out0(decoder_3_out0), .out1(decoder_3_out1), .out2(decoder_3_out2), .out3(decoder_3_out3),
    .out4(decoder_3_out4), .out5(decoder_3_out5), .out6(decoder_3_out6), .out7(decoder_3_out7), .sel(RZ));
  assign BusZ = decoder_3_out2 ? R2_q : 32'bz;  // Controlled_Buffer controlled_buffer_12
  assign BusZ = decoder_3_out3 ? R3_q : 32'bz;  // Controlled_Buffer controlled_buffer_13
  assign BusZ = decoder_3_out4 ? R4_q : 32'bz;  // Controlled_Buffer controlled_buffer_14
  assign BusZ = decoder_3_out5 ? R5_q : 32'bz;  // Controlled_Buffer controlled_buffer_15
  assign BusZ = decoder_3_out6 ? R6_q : 32'bz;  // Controlled_Buffer controlled_buffer_16
endmodule

module controlUnit (
  input  [4:0] opCode,
  input  [1:0] f,
  output [1:0] pcCalc,
  output \dist ,
  output RW,
  output ext,
  output [1:0] Bsel,
  output memoryWrite,
  output memoryRead,
  output [1:0] WBdata,
  output [3:0] ALUop
);

  ROM #(.addrWidth(5), .dataWidth(11)) rom_1 (
    .addr(opCode), .data({WBdata, memoryRead, memoryWrite, Bsel, ext, RW, \dist , pcCalc}));  // open: sel
  ROM #(.addrWidth(7), .dataWidth(4)) rom_2 (.addr({opCode, f}), .data(ALUop));  // open: sel

  // Notes on the sheet:
  //   contents of rom_1 (hex, n*v repeats v):
  //   504 1 3 2 0 4 5 6 7 101 103 102 100 505 506 507 50b 105
  //   contents of rom_2 (hex, n*v repeats v):
  //   11*0 4 1
endmodule
